# Fritzing sketch test (saved by Fritzing 0.9.3b)
circuit board: 10cm x 6cm
perfboards: 1

parts:
  J1 = Screw terminal - 2 pins [package=THT]
  J2 = screw terminal, 3 pins
  J3 = screw terminal, 3 pins
  LED1 = LED - 5mm [color="Red (633nm)" package="5 mm [THT]"]
  R1 = Resistor [tolerance=±5% resistance=220 package=THT]
  SPKR1 = Loudspeaker
  C1 = Electrolytic Capacitor [capacitance=1µF package="100 mil [THT, electrolytic]"]
  D1 = Rectifier Diode [part_number=1N4001 package="300 mil [THT]"]
  7_Segment1 = 7 Segment Display
  7_Segment2 = 7 Segment Display
  U1 = mystery part, 3 pins [chip_label=?]

nets:
  N1: J1.pin1, J2.pin2, J3.pin2, R1.Pin_0, SPKR1.pin1, C1.-, D1.anode, 7_Segment1.Segment_F, 7_Segment1.common_anode, 7_Segment1.Segment_A, 7_Segment2.common_anode, 7_Segment2.Segment_A, U1.pin1
  N2: J1.pin2, J2.pin1, J3.pin1, LED1.cathode, SPKR1.pin2, C1.+, D1.cathode, 7_Segment1.Segment_E, 7_Segment1.Segment_B, 7_Segment2.Segment_B, U1.pin2
  N3: LED1.anode, R1.Pin_1
  N4: 7_Segment1.Segment_G, 7_Segment2.Segment_DP
  N5: 7_Segment1.Segment_D, 7_Segment2.Segment_D, U1.pin3
  N6: 7_Segment1.Segment_C, 7_Segment2.Segment_C
