# Fritzing sketch test2 (saved by Fritzing 0.9.3b)
circuit board: 8.46667cm x 5.64444cm
breadboards: 1

parts:
  Raspberry_Pi_1 = Raspberry Pi 3 [part_number=RPI-3-V1.2]
  R1 = Resistor [tolerance=±5% resistance=4.7k package=THT]
  J1 = screw terminal, 3 pins
  J2 = shrouded pin header, 40 pins [form="♂ (shrouded male)"]
  J3 = screw terminal, 3 pins
  J4 = screw terminal, 3 pins
  J5 = Screw terminal - 2 pins [package=THT]
  J6 = Screw terminal - 2 pins [package=THT]
  J7 = Screw terminal - 2 pins [package=THT]
  J8 = screw terminal, 3 pins  # not connected
  Onderdeel1 = Adafruit MAX31865 RTD Sensor Breakout [part_number="Adafruit #3328"]
  J9 = female pin header, 8 pins [form="♀ (female)"]

nets:
  3V3: Raspberry_Pi_1.3v3, R1.Pin_0, J1.pin1, J2.pin1, J2.pin40, J3.pin1, J4.pin1, Onderdeel1.VIN, J9.pin1
  N1: Raspberry_Pi_1.GPIO4, R1.Pin_1, J1.pin2, J2.pin4, J2.pin37, J3.pin2, J4.pin2
  GND: Raspberry_Pi_1.GND, J1.pin3, J2.pin5, J2.pin36, J2.pin38, J3.pin3, J4.pin3, J5.pin1, J6.pin1, J7.pin1, Onderdeel1.GND, J9.pin2
  N2: J2.pin32, J7.pin2
  N3: J2.pin33, J6.pin2
  N4: J2.pin35, J5.pin2
  N5: Onderdeel1.3.3V, J9.pin3
  N6: Onderdeel1.SCLK, J9.pin4
  N7: Onderdeel1.SDO, J9.pin5
  N8: Onderdeel1.SDI, J9.pin6
  N9: Onderdeel1.CS, J9.pin7
  N10: Onderdeel1.DRDY, J9.pin8

custom parts:
  Adafruit MAX31865 RTD Sensor Breakout: For precision temperature sensing, nothing beats a Platinum RTD. Resistance temperature detectors (RTDs) are temperature sensors that contain a resistor that changes resistance value as its temperature changes, basically a kind of thermistor. In this sensor, the resistor is actually a small strip of Platinum with a resistance of 100 ohms at 0°C, thus the name PT100. Compared to most NTC/PTC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
